// Logisim project CA_Phase1.circ as structural Verilog: 5 circuits, main circuit main
module main (
  input  [15:0] in_1,
  input  in_2
);

  wire alu_1_zero, ALUSrc, beq_out, bne_out, clock_1_out, controlunit_1_brancheq, controlunit_1_branchne,
       controlunit_1_jump, MemRead, MemToReg, MemWrite, or_1_out, RegDst, REGWrite;
  wire [2:0] alucontrol_1_ctr, ALUOp;
  wire [4:0] multiplexer_2_out;
  wire [15:0] adder_1_out, Address, bit_extender_2_out, multiplexer_1_out, PC_q;
  wire [31:0] alu_1_output, bit_extender_1_out, multiplexer_3_out, multiplexer_4_out, ram_1_data,
       registerfile_1_read_data1, registerfile_1_read_data2;
  wire [31:11] rom_1_data;

  Clock clock_1 (.out(clock_1_out));
  Register #(.width(16)) PC (.D(multiplexer_1_out), .Q(PC_q), .clk(clock_1_out), .clr(in_2));  // open: en
  Adder #(.width(16)) adder_1 (.a(in_1), .b(PC_q), .out(adder_1_out));  // open: cin, cout
  ROM #(.addrWidth(16), .dataWidth(32)) rom_1 (
    .addr(PC_q), .data({rom_1_data[31:21], Address[15:11], rom_1_data[15:11], Address[10:0]}));  // open: sel
  Multiplexer #(.width(16), .enable("false")) multiplexer_1 (
    .in0(adder_1_out), .in1(Address), .out(multiplexer_1_out), .sel(or_1_out));
  Multiplexer #(.width(5), .disabled(0), .enable("false")) multiplexer_2 (
    .in0(Address[15:11]), .in1(rom_1_data[15:11]), .out(multiplexer_2_out), .sel(RegDst));
  ControlUnit controlunit_1 (
    .opcode(rom_1_data[31:26]), .RegDst(RegDst), .RegWrite(REGWrite), .MemWrite(MemWrite), .MemRead(MemRead),
    .MemToReg(MemToReg), .ALUSrc(ALUSrc), .BranchEq(controlunit_1_brancheq),
    .BranchNe(controlunit_1_branchne), .Jump(controlunit_1_jump), .ALUOp(ALUOp));
  RegisterFile registerfile_1 (
    .read_reg_1(rom_1_data[25:21]), .read_reg_2(Address[15:11]), .write_register(multiplexer_2_out),
    .write_data(multiplexer_4_out), .REG_write(REGWrite), .read_data2(registerfile_1_read_data2),
    .read_data1(registerfile_1_read_data1), .clk(clock_1_out));
  assign bit_extender_1_out = {{16{Address[15]}}, Address};  // Bit_Extender bit_extender_1
  Multiplexer #(.width(32), .enable("false")) multiplexer_3 (
    .in0(registerfile_1_read_data2), .in1(bit_extender_1_out), .out(multiplexer_3_out), .sel(ALUSrc));
  ALUControl alucontrol_1 (.ALUOp(ALUOp), .Function(Address[10:6]), .ctr(alucontrol_1_ctr));
  ALU alu_1 (
    .Input_1(registerfile_1_read_data1), .Input_2(multiplexer_3_out), .Output(alu_1_output),
    .Control(alucontrol_1_ctr), .Zero(alu_1_zero));
  and beq (beq_out, controlunit_1_brancheq, ~alu_1_zero);  // AND_Gate
  and bne (bne_out, controlunit_1_branchne, alu_1_zero);
  Bit_Extender #(.in_width(32), .\type ("sign")) bit_extender_2 (.in(alu_1_output), .out(bit_extender_2_out));
  or or_1 (or_1_out, beq_out, bne_out, controlunit_1_jump);
  RAM #(.addrWidth(16), .dataWidth(32), .bus("separate")) ram_1 (
    .addr(bit_extender_2_out), .din(registerfile_1_read_data2), .data(ram_1_data), .str(MemWrite),
    .clk(clock_1_out), .ld(MemRead));  // open: sel, clr
  Multiplexer #(.width(32), .enable("false")) multiplexer_4 (
    .in0(alu_1_output), .in1(ram_1_data), .out(multiplexer_4_out), .sel(MemToReg));

  // Notes on the sheet:
  //   100
endmodule

module ALU (
  input  [31:0] Input_1,
  input  [31:0] Input_2,
  input  [2:0] Control,
  output [31:0] Output,
  output Zero
);

  wire comparator_1_eq, comparator_1_lt;
  wire [31:0] adder_1_out, and_1_out, bit_extender_1_out, bit_extender_2_out, nor_1_out, or_1_out,
       subtractor_1_out, xor_1_out;

  Adder #(.width(32)) adder_1 (.a(Input_1), .b(Input_2), .out(adder_1_out));  // open: cin, cout
  Subtractor #(.width(32)) subtractor_1 (.a(Input_1), .b(Input_2), .out(subtractor_1_out));  // open: bin, bout
  assign and_1_out = Input_1 & Input_2;  // AND_Gate and_1, 32 bits wide
  assign or_1_out = Input_1 | Input_2;  // OR_Gate or_1, 32 bits wide
  assign nor_1_out = ~(Input_1 | Input_2);  // NOR_Gate nor_1, 32 bits wide
  assign xor_1_out = Input_2 ^ Input_1;  // XOR_Gate xor_1, 32 bits wide
  assign bit_extender_1_out = {{31{1'b0}}, comparator_1_eq};  // Bit_Extender bit_extender_1
  Comparator #(.width(32)) comparator_1 (
    .a(Input_1), .b(Input_2), .eq(comparator_1_eq), .lt(comparator_1_lt));  // open: gt
  assign bit_extender_2_out = {{31{1'b0}}, comparator_1_lt};  // Bit_Extender bit_extender_2
  and and_2 (Zero, ~Output[0], ~Output[1], ~Output[2], ~Output[3], ~Output[4], ~Output[5], ~Output[6], ~Output[7], ~Output[8], ~Output[9], ~Output[10], ~Output[11], ~Output[12], ~Output[13], ~Output[14], ~Output[15], ~Output[16], ~Output[17], ~Output[18], ~Output[19], ~Output[20], ~Output[21], ~Output[22], ~Output[23], ~Output[24], ~Output[25], ~Output[26], ~Output[27], ~Output[28], ~Output[29], ~Output[30], ~Output[31]);  // AND_Gate
  Multiplexer #(.select(3), .width(32), .disabled(0), .enable("false")) multiplexer_1 (
    .in0(adder_1_out), .in1(subtractor_1_out), .in2(and_1_out), .in3(or_1_out), .in4(nor_1_out),
    .in5(xor_1_out), .in6(bit_extender_1_out), .in7(bit_extender_2_out), .out(Output), .sel(Control));

  // Other names for the same wires on the sheet: Zero_t[31:0] = Output
endmodule

// RegFile
module RegisterFile (
  input  [4:0] read_reg_1,
  input  [4:0] read_reg_2,
  input  [4:0] write_register,
  input  REG_write,
  input  [31:0] write_data,
  input  clk,
  output [31:0] read_data2,
  output [31:0] read_data1
);

  wire and_1_out, and_2_out, and_3_out, and_4_out, and_5_out, and_6_out, and_7_out, and_8_out, and_9_out,
       and_10_out, and_11_out, and_12_out, and_13_out, and_14_out, and_15_out, and_16_out, and_17_out,
       and_18_out, and_19_out, and_20_out, and_21_out, and_22_out, and_23_out, and_24_out, and_25_out,
       and_26_out, and_27_out, and_28_out, and_29_out, and_30_out, and_31_out, and_32_out, decoder_1_out0,
       decoder_1_out1, decoder_1_out2, decoder_1_out3, decoder_1_out4, decoder_1_out5, decoder_1_out6,
       decoder_1_out7, decoder_1_out8, decoder_1_out9, decoder_1_out10, decoder_1_out11, decoder_1_out12,
       decoder_1_out13, decoder_1_out14, decoder_1_out15, decoder_1_out16, decoder_1_out17, decoder_1_out18,
       decoder_1_out19, decoder_1_out20, decoder_1_out21, decoder_1_out22, decoder_1_out23, decoder_1_out24,
       decoder_1_out25, decoder_1_out26, decoder_1_out27, decoder_1_out28, decoder_1_out29, decoder_1_out30,
       decoder_1_out31, undriven;
  wire [31:0] a0_q, a1_q, a2_q, a3_q, at_q, fp_q, gp_q, k0_q, k1_q, ra_q, s0_q, s1_q, s2_q, s3_q, s4_q, s5_q,
       s6_q, s7_q, sp_q, t0_q, t1_q, t2_q, t3_q, t4_q, t5_q, t6_q, t7_q, t8_q, t9_q, v0_q, v1_q, zero_q;

  Decoder #(.select(5), .enable("false")) decoder_1 (
    .out0(decoder_1_out0), .out1(decoder_1_out1), .out2(decoder_1_out2), .out3(decoder_1_out3),
    .out4(decoder_1_out4), .out5(decoder_1_out5), .out6(decoder_1_out6), .out7(decoder_1_out7),
    .out8(decoder_1_out8), .out9(decoder_1_out9), .out10(decoder_1_out10), .out11(decoder_1_out11),
    .out12(decoder_1_out12), .out13(decoder_1_out13), .out14(decoder_1_out14), .out15(decoder_1_out15),
    .out16(decoder_1_out16), .out17(decoder_1_out17), .out18(decoder_1_out18), .out19(decoder_1_out19),
    .out20(decoder_1_out20), .out21(decoder_1_out21), .out22(decoder_1_out22), .out23(decoder_1_out23),
    .out24(decoder_1_out24), .out25(decoder_1_out25), .out26(decoder_1_out26), .out27(decoder_1_out27),
    .out28(decoder_1_out28), .out29(decoder_1_out29), .out30(decoder_1_out30), .out31(decoder_1_out31),
    .sel(write_register));
  and and_1 (and_1_out, decoder_1_out0, REG_write);
  and and_2 (and_2_out, decoder_1_out1, REG_write);
  and and_3 (and_3_out, decoder_1_out2, REG_write);
  and and_4 (and_4_out, decoder_1_out3, REG_write);
  and and_5 (and_5_out, decoder_1_out4, REG_write);
  and and_6 (and_6_out, decoder_1_out5, REG_write);
  and and_7 (and_7_out, decoder_1_out6, REG_write);
  and and_8 (and_8_out, decoder_1_out7, REG_write);
  Register #(.width(32)) zero (.D(write_data), .Q(zero_q), .clk(undriven), .clr(and_1_out));  // open: en
  Register #(.width(32)) at (.D(write_data), .Q(at_q), .clk(undriven), .clr(and_2_out));  // open: en
  Register #(.width(32)) v0 (.D(write_data), .Q(v0_q), .clk(undriven), .clr(and_3_out));  // open: en
  Register #(.width(32)) v1 (.D(write_data), .Q(v1_q), .clk(undriven), .clr(and_4_out));  // open: en
  Register #(.width(32)) a0 (.D(write_data), .Q(a0_q), .clk(undriven), .clr(and_5_out));  // open: en
  Register #(.width(32)) a1 (.D(write_data), .Q(a1_q), .clk(undriven), .clr(and_6_out));  // open: en
  Register #(.width(32)) a2 (.D(write_data), .Q(a2_q), .clk(undriven), .clr(and_7_out));  // open: en
  Register #(.width(32)) a3 (.D(write_data), .Q(a3_q), .clk(undriven), .clr(and_8_out));  // open: en
  and and_9 (and_9_out, decoder_1_out8, REG_write);
  and and_10 (and_10_out, decoder_1_out9, REG_write);
  and and_11 (and_11_out, decoder_1_out10, REG_write);
  and and_12 (and_12_out, decoder_1_out11, REG_write);
  and and_13 (and_13_out, decoder_1_out12, REG_write);
  and and_14 (and_14_out, decoder_1_out13, REG_write);
  and and_15 (and_15_out, decoder_1_out14, REG_write);
  and and_16 (and_16_out, decoder_1_out15, REG_write);
  Register #(.width(32)) t0 (.D(write_data), .Q(t0_q), .clk(undriven), .clr(and_9_out));  // open: en
  Register #(.width(32)) t1 (.D(write_data), .Q(t1_q), .clk(undriven), .clr(and_10_out));  // open: en
  Register #(.width(32)) t2 (.D(write_data), .Q(t2_q), .clk(undriven), .clr(and_11_out));  // open: en
  Register #(.width(32)) t3 (.D(write_data), .Q(t3_q), .clk(undriven), .clr(and_12_out));  // open: en
  Register #(.width(32)) t4 (.D(write_data), .Q(t4_q), .clk(undriven), .clr(and_13_out));  // open: en
  Register #(.width(32)) t5 (.D(write_data), .Q(t5_q), .clk(undriven), .clr(and_14_out));  // open: en
  Register #(.width(32)) t6 (.D(write_data), .Q(t6_q), .clk(undriven), .clr(and_15_out));  // open: en
  Register #(.width(32)) t7 (.D(write_data), .Q(t7_q), .clk(undriven), .clr(and_16_out));  // open: en
  and and_17 (and_17_out, decoder_1_out16, REG_write);
  and and_18 (and_18_out, decoder_1_out17, REG_write);
  and and_19 (and_19_out, decoder_1_out18, REG_write);
  and and_20 (and_20_out, decoder_1_out19, REG_write);
  and and_21 (and_21_out, decoder_1_out20, REG_write);
  and and_22 (and_22_out, decoder_1_out21, REG_write);
  and and_23 (and_23_out, decoder_1_out22, REG_write);
  and and_24 (and_24_out, decoder_1_out23, REG_write);
  Register #(.width(32)) s0 (.D(write_data), .Q(s0_q), .clk(undriven), .clr(and_17_out));  // open: en
  Register #(.width(32)) s1 (.D(write_data), .Q(s1_q), .clk(undriven), .clr(and_18_out));  // open: en
  Register #(.width(32)) s2 (.D(write_data), .Q(s2_q), .clk(undriven), .clr(and_19_out));  // open: en
  Register #(.width(32)) s3 (.D(write_data), .Q(s3_q), .clk(undriven), .clr(and_20_out));  // open: en
  Register #(.width(32)) s4 (.D(write_data), .Q(s4_q), .clk(undriven), .clr(and_21_out));  // open: en
  Register #(.width(32)) s5 (.D(write_data), .Q(s5_q), .clk(undriven), .clr(and_22_out));  // open: en
  Register #(.width(32)) s6 (.D(write_data), .Q(s6_q), .clk(undriven), .clr(and_23_out));  // open: en
  Register #(.width(32)) s7 (.D(write_data), .Q(s7_q), .clk(undriven), .clr(and_24_out));  // open: en
  and and_25 (and_25_out, decoder_1_out24, REG_write);
  and and_26 (and_26_out, decoder_1_out25, REG_write);
  and and_27 (and_27_out, decoder_1_out26, REG_write);
  and and_28 (and_28_out, decoder_1_out27, REG_write);
  and and_29 (and_29_out, decoder_1_out28, REG_write);
  and and_30 (and_30_out, decoder_1_out29, REG_write);
  and and_31 (and_31_out, decoder_1_out30, REG_write);
  and and_32 (and_32_out, decoder_1_out31, REG_write);
  Register #(.width(32)) t8 (.D(write_data), .Q(t8_q), .clk(undriven), .clr(and_25_out));  // open: en
  Register #(.width(32)) t9 (.D(write_data), .Q(t9_q), .clk(undriven), .clr(and_26_out));  // open: en
  Register #(.width(32)) k0 (.D(write_data), .Q(k0_q), .clk(undriven), .clr(and_27_out));  // open: en
  Register #(.width(32)) k1 (.D(write_data), .Q(k1_q), .clk(undriven), .clr(and_28_out));  // open: en
  Register #(.width(32)) gp (.D(write_data), .Q(gp_q), .clk(undriven), .clr(and_29_out));  // open: en
  Register #(.width(32)) sp (.D(write_data), .Q(sp_q), .clk(undriven), .clr(and_30_out));  // open: en
  Register #(.width(32)) fp (.D(write_data), .Q(fp_q), .clk(undriven), .clr(and_31_out));  // open: en
  Register #(.width(32)) ra (.D(write_data), .Q(ra_q), .clk(undriven), .clr(and_32_out));  // open: en
  Multiplexer #(.select(5), .width(32), .enable("false")) multiplexer_1 (
    .in0(zero_q), .in1(at_q), .in2(v0_q), .in3(v1_q), .in4(a0_q), .in5(a1_q), .in6(a2_q), .in7(a3_q),
    .in8(t0_q), .in9(t1_q), .in10(t2_q), .in11(t3_q), .in12(t4_q), .in13(t5_q), .in14(t6_q), .in15(t7_q),
    .in16(s0_q), .in17(s1_q), .in18(s2_q), .in19(s3_q), .in20(s4_q), .in21(s5_q), .in22(s6_q), .in23(s7_q),
    .in24(t8_q), .in25(t9_q), .in26(k0_q), .in27(k1_q), .in28(gp_q), .in29(sp_q), .in30(fp_q), .in31(ra_q),
    .out(read_data1), .sel(read_reg_1));
  Multiplexer #(.select(5), .width(32), .enable("false")) multiplexer_2 (
    .in0(zero_q), .in1(at_q), .in2(v0_q), .in3(v1_q), .in4(a0_q), .in5(a1_q), .in6(a2_q), .in7(a3_q),
    .in8(t0_q), .in9(t1_q), .in10(t2_q), .in11(t3_q), .in12(t4_q), .in13(t5_q), .in14(t6_q), .in15(t7_q),
    .in16(s0_q), .in17(s1_q), .in18(s2_q), .in19(s3_q), .in20(s4_q), .in21(s5_q), .in22(s6_q), .in23(s7_q),
    .in24(t8_q), .in25(t9_q), .in26(k0_q), .in27(k1_q), .in28(gp_q), .in29(sp_q), .in30(fp_q), .in31(ra_q),
    .out(read_data2), .sel(read_reg_2));
endmodule

module ControlUnit (
  input  [5:0] opcode,
  output RegDst,
  output RegWrite,
  output MemWrite,
  output MemRead,
  output MemToReg,
  output ALUSrc,
  output BranchEq,
  output BranchNe,
  output Jump,
  output [2:0] ALUOp
);

  wire addi_out, andi_out, ori_out;

  not R_type (RegDst, opcode[5]);
  and addi (addi_out, opcode[5], ~opcode[4], ~opcode[3], ~opcode[2], ~opcode[1], ~opcode[0]);  // AND_Gate
  and lw (MemRead, opcode[5], ~opcode[4], ~opcode[3], ~opcode[2], ~opcode[1], opcode[0]);  // AND_Gate
  and sw (MemWrite, opcode[5], ~opcode[4], ~opcode[3], ~opcode[2], opcode[1], ~opcode[0]);  // AND_Gate
  and andi (andi_out, opcode[5], ~opcode[4], ~opcode[3], ~opcode[2], opcode[1], opcode[0]);  // AND_Gate
  and ori (ori_out, opcode[5], ~opcode[4], ~opcode[3], opcode[2], ~opcode[1], ~opcode[0]);  // AND_Gate
  and beq (BranchEq, opcode[5], ~opcode[4], ~opcode[3], opcode[2], ~opcode[1], opcode[0]);  // AND_Gate
  and bne (BranchNe, opcode[5], ~opcode[4], ~opcode[3], opcode[2], opcode[1], ~opcode[0]);  // AND_Gate
  and u_jump (Jump, opcode[5], opcode[4], opcode[3], opcode[2], opcode[1], opcode[0]);
  or or_1 (RegWrite, addi_out, MemRead, RegDst, andi_out, ori_out);
  or or_2 (ALUSrc, addi_out, MemRead, MemWrite, andi_out, ori_out);
  nor nor_1 (ALUOp[0], BranchEq, ori_out, MemWrite, RegDst);
  nor nor_2 (ALUOp[1], MemWrite, MemRead, addi_out, RegDst);
  nor nor_3 (ALUOp[2], ori_out, andi_out, addi_out, RegDst);

  assign MemToReg = MemRead;
endmodule

module ALUControl (
  input  [4:0] Function,
  input  [2:0] ALUOp,
  output [2:0] ctr
);

  wire _0_1_0_out, _0_1_1_out, _0000_out, _1_1_0_out, _1_1_1_out, _1000_out, _1010_out, _1011_out, _1100_out,
       _1101_out, _1110_out, is_I_out, is_R_out, not_1_out, not_2_out, not_3_out, not_4_out, not_5_out,
       not_6_out, not_7_out;

  and is_R (is_R_out, not_1_out, not_2_out, not_3_out);
  not is_I (is_I_out, is_R_out);
  not not_1 (not_1_out, ALUOp[2]);
  not not_2 (not_2_out, ALUOp[1]);
  not not_3 (not_3_out, ALUOp[0]);
  and _0_1_0 (_0_1_0_out, is_I_out, not_1_out, ALUOp[1], not_3_out);
  and _0_1_1 (_0_1_1_out, is_I_out, not_1_out, ALUOp[1], ALUOp[0]);
  or or_1 (ctr[2], _1_1_0_out, _1_1_1_out, _0000_out, _1010_out, _1011_out, _1000_out);
  and _1_1_0 (_1_1_0_out, is_I_out, ALUOp[2], ALUOp[1], not_3_out);
  and _1_1_1 (_1_1_1_out, is_I_out, ALUOp[2], ALUOp[1], ALUOp[0]);
  or or_2 (ctr[1], _1_1_1_out, _1_1_0_out, _0_1_1_out, _0_1_0_out, _0000_out, _1000_out, _1101_out, _1100_out);
  not not_4 (not_4_out, Function[3]);
  not not_5 (not_5_out, Function[1]);
  not not_6 (not_6_out, Function[2]);
  or or_3 (ctr[0], _0_1_0_out, _1010_out, _1000_out, _1100_out, _1110_out);
  not not_7 (not_7_out, Function[0]);
  and _1110 (_1110_out, is_R_out, Function[3], Function[2], Function[1], not_7_out);
  and _1100 (_1100_out, is_R_out, Function[3], Function[2], not_5_out, not_7_out);
  and _1101 (_1101_out, is_R_out, Function[3], Function[2], not_5_out, Function[0]);
  and _1000 (_1000_out, is_R_out, Function[3], not_6_out, not_5_out, not_7_out);
  and _1011 (_1011_out, is_R_out, Function[3], not_6_out, Function[1], Function[0]);
  and _1010 (_1010_out, is_R_out, Function[3], not_6_out, Function[1], not_7_out);
  and _0000 (_0000_out, is_R_out, not_4_out, not_6_out, not_5_out, not_7_out);

  // Notes on the sheet:
  //   0
endmodule
